# Fritzing sketch full (saved by Fritzing 0.9.3b)
breadboards: 1

parts:
  SD_card_module1 = SD Card Module
  Part1 = Arduino Uno (Rev3)
  Mod1 = KY-015 Temperature & Humidity Sensor Module [package="Breakout board"]
  J1 = Piezo Speaker
  R1 = Resistor [tolerance=±5% resistance=220 package=THT]

nets:
  N1: SD_card_module1.+3.3, Part1.3V3
  N2: SD_card_module1.CS, Part1.D4
  N3: SD_card_module1.MOSI, Part1.D10_PWM/SS
  N4: SD_card_module1.SCK, Part1.D13/SCK
  N5: SD_card_module1.MISO, Part1.D12/MISO
  GND: SD_card_module1.GND, Part1.GND, Mod1.S, J1.pin1
  N6: Part1.A0, Mod1.Vin
  N7: Part1.D6_PWM, R1.Pin_0
  N8: J1.pin2, R1.Pin_1

notes:
  DHT11 Module
  SD card Module
  Halil
  Gök

custom parts:
  SD Card Module: SD Card Module Slot Socket Reader For Arduino ARM MCU
  KY-015 Temperature & Humidity Sensor Module: KY-015 temperature and humidity sensor module, provides a low-latency serial interface to measure humidity and temperature.
